# Fritzing sketch lora_receiver (saved by Fritzing 1.0.5)
breadboards: 1

parts:
  S1 = Pushbutton [package="[THT]"]
  Mod1 = Raspberry Pi Pico
  IC2 = ULN2003A [package="DIP16 [THT]"]
  IC3 = ULN2003A [package="DIP16 [THT]"]
  IC4 = ULN2003A [package="DIP16 [THT]"]
  IC5 = ULN2003A [package="DIP16 [THT]"]
  Part1 = Lilypad Battery Connect

nets:
  N1: S1.Pin_1, S1.Pin_2
  N2: S1.Pin_3, S1.Pin_4, Mod1.pin_30
  N3: Mod1.pin_3, Mod1.pin_8, Mod1.pin_13, Mod1.pin_18, Mod1.pin_23, Mod1.pin_28, Mod1.pin_33, Mod1.pin_38, Mod1.pin_42, IC2.Out_1, IC3.Out_1, IC4.Out_1, IC5.Out_1
  N4: Mod1.pin_4, IC2.In_5
  N5: Mod1.pin_5, IC2.In_6
  N6: Mod1.pin_6, Part1.+
  N7: Mod1.pin_7, Part1.-
  N8: Mod1.pin_9, IC2.In_7
  N9: Mod1.pin_10, IC2.0V
  N10: Mod1.pin_14, IC3.In_5
  N11: Mod1.pin_15, IC3.In_6
  N12: Mod1.pin_19, IC3.In_7
  N13: Mod1.pin_20, IC3.0V
  N14: Mod1.pin_24, IC4.In_5
  N15: Mod1.pin_25, IC4.In_6
  N16: Mod1.pin_26, IC4.In_7
  N17: Mod1.pin_27, IC4.0V
  N18: Mod1.pin_29, IC5.In_5
  N19: Mod1.pin_31, IC5.In_6
  N20: Mod1.pin_32, IC5.In_7
  N21: Mod1.pin_34, IC5.0V
  N22: Mod1.pin_40, IC2.Out_2, IC3.Out_2, IC4.Out_2, IC5.Out_2

custom parts:
  Raspberry Pi Pico: Raspberry Pi Pico. Based around the RP2040 microcontroller the Pico is a low cost microcontroller device bringing Raspberry Pi quality, cost, and easy of use to the microcontroller space. Jan 2021, Split part in to two versions: tht (this one) and SMD. This one will drill holes for a .1 in header in pcb to allow plugging in the module as well as providing pads to solder the module to the top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
