# Fritzing sketch lora_transmitter (saved by Fritzing 1.0.5)
breadboards: 1

parts:
  S1 = Pushbutton [package="[THT]"]
  Mod1 = Raspberry Pi Pico
  Part1 = Lilypad Battery Connect
  S2 = Pushbutton [package="[THT]"]
  S3 = Pushbutton [package="[THT]"]  # not connected
  S4 = Pushbutton [package="[THT]"]  # not connected
  S5 = Pushbutton [package="[THT]"]

nets:
  N1: S1.Pin_1, S1.Pin_2, S2.Pin_1, S2.Pin_2, S5.Pin_1, S5.Pin_2
  N2: S1.Pin_3, S1.Pin_4, Mod1.pin_30
  N3: Mod1.pin_3, Mod1.pin_8, Mod1.pin_13, Mod1.pin_18, Mod1.pin_23, Mod1.pin_28, Mod1.pin_33, Mod1.pin_38
  N4: Mod1.pin_4, S5.Pin_3, S5.Pin_4
  N5: Mod1.pin_5, S2.Pin_3, S2.Pin_4
  N6: Mod1.pin_6, Part1.+
  N7: Mod1.pin_7, Part1.-

custom parts:
  Raspberry Pi Pico: Raspberry Pi Pico. Based around the RP2040 microcontroller the Pico is a low cost microcontroller device bringing Raspberry Pi quality, cost, and easy of use to the microcontroller space. Jan 2021, Split part in to two versions: tht (this one) and SMD. This one will drill holes for a .1 in header in pcb to allow plugging in the module as well as providing pads to solder the module to the top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
